# Fritzing sketch LEDTest (saved by Fritzing 0.9.3b)
breadboards: 1

parts:
  Part1 = RedBear-Duo
  Q1 = Basic FET N-Channel [package="TO220 [THT]"]
  R1 = Resistor [tolerance=±5% resistance=220 package=THT]
  LED1 = LED - 5mm [color="Red (633nm)" package="5 mm [THT]"]

nets:
  N1: Part1.GND, Q1.gate, R1.Pin_1
  N2: Part1.D2, Q1.drain, R1.Pin_0
  N3: Part1.3V3, LED1.anode
  N4: Q1.source, LED1.cathode

custom parts:
  RedBear-Duo: Duo is a thumb-size development board made to simplify the building process of Internet of Things (IoT). This part is a modification of the Particle Photon part by Brett Walach,Fabian Althaus
