# Fritzing sketch SoundBoard (saved by Fritzing 0.9.3b)
circuit board: 3.21132cm x 2.265cm
breadboards: 1

parts:
  Player = DFRobot DFPlayer Mini [part_number=DFR0299]
  ControllerBoard = male pin header, 4 pins [form="♂ (male)"]
  Speaker = male pin header, 3 pins [form="♂ (male)"]

nets:
  N1: Player.VCC, ControllerBoard.pin1
  N2: Player.RX, ControllerBoard.pin4
  N3: Player.TX, ControllerBoard.pin3
  N4: Player.SPK_1, Speaker.pin2
  N5: Player.GND-1, Player.GND-2, ControllerBoard.pin2, Speaker.pin1
  N6: Player.SPK_2, Speaker.pin3
