# Fritzing sketch TruckController (saved by Fritzing 0.9.3b)
circuit board: 7.85068cm x 4.1058cm

parts:
  Steering = Dagu DGServo 9g header (male) [package=THT]
  Gearbox = Dagu DGServo 9g header (male) [package=THT]
  FFT1 = MOSFET-NCHANNEL [package=to220v]
  R1 = Resistor [tolerance=±5% resistance=10k package=THT]
  BackLights = male pin header, 5 pins [form="♂ (male)"]
  TrailerLights = male pin header, 5 pins [form="♂ (male)"]
  FrontLights = male pin header, 6 pins [form="♂ (male)"]
  SidePos = male pin header, 2 pins [form="♂ (male)"]
  TopPos = male pin header, 2 pins [form="♂ (male)"]
  FFT2 = MOSFET-NCHANNEL [package=to220v]
  R2 = Resistor [tolerance=±5% resistance=10k package=THT]
  FFT3 = MOSFET-NCHANNEL [package=to220v]
  FFT5 = MOSFET-NCHANNEL [package=to220v]
  FFT6 = MOSFET-NCHANNEL [package=to220v]
  FFT7 = MOSFET-NCHANNEL [package=to220v]
  R3 = Resistor [tolerance=±5% resistance=10k package=THT]
  R4 = Resistor [tolerance=±5% resistance=10k package=THT]
  R5 = Resistor [tolerance=±5% resistance=10k package=THT]
  R6 = Resistor [tolerance=±5% resistance=10k package=THT]
  R7 = Resistor [tolerance=±5% resistance=10k package=THT]
  FFT8 = MOSFET-NCHANNEL [package=to220v]
  R8 = Resistor [tolerance=±5% resistance=10k package=THT]
  SideIndicators = male pin header, 3 pins [form="♂ (male)"]
  FFT4 = MOSFET-NCHANNEL [package=to220v]
  Sound = male pin header, 4 pins [form="♂ (male)"]
  RedBear_Duo = RedBear-Duo
  ESC = Dagu DGServo 9g header (male) [package=THT]
  C1 = Ceramic Capacitor [capacitance="100 nF" package="1206 [SMD, multilayer]"]
  Aux = Dagu DGServo 9g header (male) [package=THT]
  U2 = Voltage Regulator - 3.3V [package="TO220 [THT]"]
  C2 = Electrolytic Capacitor [capacitance=10μF package="100 mil [THT, electrolytic]"]

nets:
  GND: Steering.gnd, Gearbox.gnd, FFT1.S, R1.Pin_1, FFT2.S, R2.Pin_1, FFT3.S, FFT5.S, FFT6.S, FFT7.S, R3.Pin_1, R4.Pin_1, R5.Pin_1, R6.Pin_1, R7.Pin_1, FFT8.S, R8.Pin_1, FFT4.S, Sound.pin2, RedBear_Duo.GND, ESC.gnd, C1.0, Aux.gnd, U2.GND, C2.-
  VCC: Steering.Vcc, Gearbox.Vcc, BackLights.pin1, TrailerLights.pin1, FrontLights.pin1, SidePos.pin1, TopPos.pin1, SideIndicators.pin1, Sound.pin1, RedBear_Duo.3V3, Aux.Vcc, U2.output_voltage, C2.+
  N1: Steering.pulse, RedBear_Duo.A4
  N2: Gearbox.pulse, RedBear_Duo.A5
  N3: FFT1.G, R1.Pin_0, RedBear_Duo.D6
  N4: FFT1.D, SidePos.pin2, TopPos.pin2
  N5: BackLights.pin2, TrailerLights.pin2, FFT2.D
  N6: BackLights.pin3, TrailerLights.pin3, FFT7.D
  N7: BackLights.pin4, TrailerLights.pin4, FrontLights.pin4, FFT6.D, SideIndicators.pin2
  N8: BackLights.pin5, TrailerLights.pin5, FrontLights.pin5, FFT5.D, SideIndicators.pin3
  N9: FrontLights.pin2, FFT4.D
  N10: FrontLights.pin3, FFT3.D
  N11: FrontLights.pin6, FFT8.D
  N12: FFT2.G, R2.Pin_0, RedBear_Duo.D5
  N13: FFT3.G, R3.Pin_0, RedBear_Duo.D4
  N14: FFT5.G, R5.Pin_0, RedBear_Duo.D2
  N15: FFT6.G, R6.Pin_0, RedBear_Duo.D1
  N16: FFT7.G, R7.Pin_0, RedBear_Duo.D0
  N17: R4.Pin_0, FFT4.G, RedBear_Duo.D3
  N18: FFT8.G, R8.Pin_0, RedBear_Duo.D7
  N19: Sound.pin3, RedBear_Duo.TX
  N20: Sound.pin4, RedBear_Duo.RX
  N21: RedBear_Duo.A0, Aux.pulse
  N22: RedBear_Duo.DAC, ESC.pulse
  N23: ESC.Vcc, C1.1, U2.input_voltage

notes:
  Truck Controller V1.1
  (c) Thomas Proffen, 2018
  +
  Revision 1.1 - Added V regulator / AUX port

custom parts:
  RedBear-Duo: Duo is a thumb-size development board made to simplify the building process of Internet of Things (IoT). This part is a modification of the Particle Photon part by Brett Walach,Fabian Althaus
